// Digital circuit fpga.dig as structural Verilog
module fpga (
  input  push,
  input  [15:0] i,
  input  pop,
  input  we_tos,
  output [15:0] o,
  output [15:0] o_2,
  output [11:0] o_3,
  output [15:0] o_4
);

  wire c, or_1_out;
  wire [11:0] add_1_s, multiplexer_1_out, sp_q;
  wire [15:0] multiplexer_3_out, multiplexer_4_out;

  Button button_1 (.out(c));
  Multiplexer #(.Bits(12)) multiplexer_1 (.sel(pop), .in_0(12'h1), .in_1({12{1'b1}}), .out(multiplexer_1_out));
  Add #(.Bits(12)) add_1 (.a(sp_q), .b(multiplexer_1_out), .c_i(1'b0), .s(add_1_s));  // open: c_o
  or or_1 (or_1_out, push, pop);
  Register #(.Bits(12)) sp (.D(add_1_s), .C(c), .en(or_1_out), .Q(sp_q));
  Multiplexer #(.Bits(12)) multiplexer_2 (.sel(push), .in_0(add_1_s), .in_1(sp_q), .out(o_3));
  Multiplexer #(.Bits(16)) multiplexer_3 (.sel(pop), .in_0(i), .in_1(o_4), .out(multiplexer_3_out));
  Multiplexer #(.Bits(16)) multiplexer_4 (.sel(pop), .in_0(o_2), .in_1(o), .out(multiplexer_4_out));
  Register #(.Bits(16)) top_of_stack (.D(multiplexer_3_out), .C(c), .en(we_tos), .Q(o_2));
  Register #(.Bits(16)) next_on_stack (.D(multiplexer_4_out), .C(c), .en(or_1_out), .Q(o_4));
  RAMDualPort #(.AddrBits(12), .Bits(16)) stack (.A(o_3), .Din(o_4), .str(push), .C(c), .ld(1'b1), .D(o));
endmodule
